// Logisim project Exer1.circ as structural Verilog: 1 circuit, main circuit main
module main (
  input  P,
  input  Q,
  input  R
);

  wire and_1_out, and_2_out, not_1_out, not_2_out, not_3_out, or_1_out, or_2_out;

  not not_1 (not_1_out, P);
  not not_2 (not_2_out, R);
  or or_1 (or_1_out, not_1_out, Q);
  and and_1 (and_1_out, Q, not_2_out);
  or or_2 (or_2_out, P, or_1_out);
  not not_3 (not_3_out, and_1_out);
  and and_2 (and_2_out, or_2_out, not_3_out);
  LED led_1 (.in(and_2_out));
endmodule
