// Logisim project Exer2.circ as structural Verilog: 1 circuit, main circuit main
module main (
  input  S,
  input  P,
  input  R,
  input  Q
);

  wire and_1_out, and_2_out, and_3_out, not_1_out, not_2_out, not_3_out, or_1_out, or_2_out, or_3_out;

  not not_1 (not_1_out, P);
  not not_2 (not_2_out, R);
  not not_3 (not_3_out, S);
  and and_1 (and_1_out, P, not_2_out);
  or or_1 (or_1_out, R, Q);
  or or_2 (or_2_out, not_3_out, and_1_out);
  or or_3 (or_3_out, or_1_out, not_1_out);
  and and_2 (and_2_out, or_2_out, and_3_out);
  and and_3 (and_3_out, or_3_out, S);
  LED led_1 (.in(and_2_out));

  // Notes on the sheet:
  //   E1
endmodule
