// Logisim project Exer2Pt2.circ as structural Verilog: 1 circuit, main circuit main
module main (
  input  P,
  input  Q,
  input  R,
  input  S
);

  wire and_1_out, not_1_out, not_2_out, or_1_out, or_2_out;

  not not_1 (not_1_out, R);
  and and_1 (and_1_out, P, Q, not_1_out, S);
  or or_1 (or_1_out, Q, P);
  not not_2 (not_2_out, or_1_out);
  or or_2 (or_2_out, and_1_out, not_2_out);
  LED led_1 (.in(or_2_out));

  // Notes on the sheet:
  //   E2
endmodule
