// Logisim project Inicial.circ as structural Verilog: 1 circuit, main circuit main
module main (
  input  P,
  input  Q,
  input  R
);

  wire and_1_out, not_1_out, not_2_out, not_3_out, or_1_out, or_2_out, or_3_out, or_4_out;

  not not_1 (not_1_out, P);
  not not_2 (not_2_out, Q);
  or or_1 (or_1_out, not_1_out, Q);
  or or_2 (or_2_out, not_2_out, R);
  and and_1 (and_1_out, or_1_out, or_2_out);
  or or_3 (or_3_out, R, not_1_out);
  not not_3 (not_3_out, and_1_out);
  or or_4 (or_4_out, not_3_out, or_3_out);
  LED led_1 (.in(or_4_out));
endmodule
